// Logisim project control_logic.circ as structural Verilog: 4 circuits, main circuit control_logic
module control_logic (
  input  [31:0] inst,
  input  BrEq,
  input  BrLt,
  output PCSel,
  output RegWEn,
  output [2:0] ImmSel,
  output BrUn,
  output ASel,
  output BSel,
  output [3:0] ALUSel,
  output MemRW,
  output [1:0] WBSel,
  output CSRSel,
  output CSRWen
);


  assign ALUSel = 4'b0000;
  assign ASel = 1'b0;
  assign BrUn = 1'b0;
  assign BSel = 1'b0;
  assign CSRSel = 1'b0;
  assign CSRWen = 1'b0;
  assign ImmSel = 3'b000;
  assign MemRW = 1'b0;
  assign PCSel = 1'b0;
  assign RegWEn = 1'b0;
  assign WBSel = 2'b00;

  // Notes on the sheet:
  //   INPUTS to your circuit
  //   DON'T CHANGE THE LOCATIONS OF THE INPUTS AND OUTPUTS!
  //   OUTPUT from your circuit
endmodule

module ASel0 (
  input  [4:0] opcode,
  output ASEL_Output
);

  wire AND0_out, AND1_out, AND2_out, not_1_out, not_2_out, not_3_out, not_4_out, not_5_out, not_6_out,
       not_7_out;

  not not_1 (not_1_out, opcode[0]);
  not not_2 (not_2_out, opcode[1]);
  not not_3 (not_3_out, opcode[2]);
  not not_4 (not_4_out, opcode[1]);
  not not_5 (not_5_out, opcode[3]);
  not not_6 (not_6_out, opcode[4]);
  not not_7 (not_7_out, opcode[2]);
  and AND0 (AND0_out, not_1_out, not_2_out, not_3_out, opcode[3], opcode[4]);
  and AND1 (AND1_out, opcode[0], not_4_out, opcode[2], not_5_out, not_6_out);
  // Probe on AND1_out
  and AND2 (AND2_out, opcode[0], opcode[1], not_7_out, opcode[3], opcode[4]);
  or or_1 (ASEL_Output, AND0_out, AND1_out, AND2_out);

  // Other names for the same wires on the sheet: A0 = opcode[0]; A1 = opcode[1]; A2 = opcode[2]; A3 = opcode[3];
  //   A4 = opcode[4]
endmodule

module PCSel0 (
  input  BrEq,
  input  [4:0] opcode,
  input  BrLt,
  input  [2:0] funct3,
  output PCSel_Output
);

  wire and_6_out, BEQ, BGE, BGEU, BLT, BLTU, BNE, I_JALR, not_1_out, not_2_out, not_3_out, not_4_out,
       not_5_out, not_6_out, not_7_out, not_8_out, not_9_out, not_10_out, not_11_out, not_12_out, not_13_out,
       not_14_out, not_15_out, not_16_out, not_17_out, not_18_out, not_19_out, not_20_out, not_21_out,
       not_22_out, not_23_out, or_1_out, SB, UJ;

  not not_1 (not_1_out, opcode[0]);
  not not_2 (not_2_out, opcode[1]);
  not not_3 (not_3_out, opcode[2]);
  not not_4 (not_4_out, opcode[1]);
  not not_5 (not_5_out, opcode[2]);
  not not_6 (not_6_out, funct3[0]);
  not not_7 (not_7_out, funct3[1]);
  not not_8 (not_8_out, funct3[2]);
  not not_9 (not_9_out, funct3[0]);
  not not_10 (not_10_out, funct3[1]);
  not not_11 (not_11_out, funct3[2]);
  not not_12 (not_12_out, funct3[0]);
  not not_13 (not_13_out, funct3[1]);
  not not_14 (not_14_out, funct3[0]);
  and and_1 (SB, not_1_out, not_2_out, not_3_out, opcode[3], opcode[4]);
  and and_2 (I_JALR, opcode[0], not_4_out, not_5_out, opcode[3], opcode[4], not_6_out, not_7_out, not_8_out);
  and and_3 (BEQ, not_9_out, not_10_out, not_11_out, BrEq);
  and and_4 (BLT, not_12_out, not_13_out, funct3[2], BrLt);
  and and_5 (BLTU, not_14_out, funct3[1], funct3[2], BrLt);
  or or_1 (or_1_out, BEQ, BLT, BLTU, BNE, BGE, BGEU);
  and and_6 (and_6_out, or_1_out, SB);
  not not_15 (not_15_out, opcode[2]);
  not not_16 (not_16_out, funct3[1]);
  not not_17 (not_17_out, funct3[2]);
  not not_18 (not_18_out, BrEq);
  not not_19 (not_19_out, funct3[1]);
  not not_20 (not_20_out, BrEq);
  not not_21 (not_21_out, BrLt);
  not not_22 (not_22_out, BrEq);
  not not_23 (not_23_out, BrLt);
  or or_2 (PCSel_Output, and_6_out, I_JALR, UJ);
  and and_7 (UJ, opcode[0], opcode[1], not_15_out, opcode[3], opcode[4]);
  and and_8 (BNE, funct3[0], not_16_out, not_17_out, not_18_out);
  and and_9 (BGE, funct3[0], not_19_out, funct3[2], not_20_out, not_21_out);
  and and_10 (BGEU, funct3[0], funct3[1], funct3[2], not_22_out, not_23_out);

  // Other names for the same wires on the sheet: B0 = funct3[0]; B1 = funct3[1]; B2 = funct3[2]; A0 = opcode[0];
  //   A1 = opcode[1]; A2 = opcode[2]; A3 = opcode[3]; A4 = opcode[4]
endmodule

module BrUn0 (
  input  [4:0] opcode,
  input  [2:0] funct3,
  output BrUn_Output
);

  wire BGEU, BLTU, not_1_out, not_2_out, not_3_out, not_4_out, or_1_out, SB;

  not not_1 (not_1_out, opcode[0]);
  not not_2 (not_2_out, opcode[1]);
  not not_3 (not_3_out, opcode[2]);
  not not_4 (not_4_out, funct3[0]);
  or or_1 (or_1_out, BLTU, BGEU);
  and and_1 (SB, not_1_out, not_2_out, not_3_out, opcode[3], opcode[4]);
  and and_2 (BLTU, not_4_out, funct3[1], funct3[2]);
  and and_3 (BrUn_Output, SB, or_1_out);
  and and_4 (BGEU, funct3[0], funct3[1], funct3[2]);

  // Other names for the same wires on the sheet: B0 = funct3[0]; B1 = funct3[1]; B2 = funct3[2]; A0 = opcode[0];
  //   A1 = opcode[1]; A2 = opcode[2]; A3 = opcode[3]; A4 = opcode[4]
endmodule
