// Logisim project cpu.circ as structural Verilog: 3 circuits, main circuit cpu
module cpu (
  input  clk,
  input  [31:0] INSTRUCTION,
  input  [31:0] READ_DATA,
  output [31:0] WRITE_ADDRESS,
  output [31:0] PROGRAM_COUNTER,
  output [31:0] ra,
  output [31:0] sp,
  output [31:0] t0,
  output [31:0] t1,
  output [31:0] t2,
  output [31:0] s0,
  output [31:0] s1,
  output [31:0] a0,
  output [31:0] tohost,
  output [3:0] WRITE_ENABLE,
  output [31:0] WRITE_DATA
);

  wire [4:0] rd, rs1, rs2;
  wire [31:0] adder_1_out, alu_result, imm, INSTRUCTION_EX, PROGRAM_COUNTER_EX, read_data_1, read_data_2;

  Adder #(.width(32)) adder_1 (.a(PROGRAM_COUNTER), .b(32'h4), .out(adder_1_out));  // open: cin, cout
  Register #(.width(32)) PC (.D(adder_1_out), .clk(clk), .Q(PROGRAM_COUNTER));  // open: en, clr
  decode decode_1 (.INST(INSTRUCTION_EX), .RD(rd), .RS1(rs1), .RS2(rs2));
  imm_gen imm_gen_1 (.inst(INSTRUCTION_EX), .ImmSel(3'b000), .imm(imm));
  // control_logic control_logic_1: pin names not known
  regfile regfile_1 (
    .rs1(rs1), .rs2(rs2), .rd(rd), .Write_Data(WRITE_DATA), .RegWEn(1'b1), .clk(clk), .ra(ra), .sp(sp),
    .t0(t0), .t1(t1), .t2(t2), .s0(s0), .s1(s1), .a0(a0), .Read_Data_1(read_data_1), .Read_Data_2(read_data_2));
  // branch_comp branch_comp_1: pin names not known
  IF_EX if_ex_1 (
    .PC_IN(PROGRAM_COUNTER), .INST_IN(INSTRUCTION), .PC_OUT(PROGRAM_COUNTER_EX), .INST_OUT(INSTRUCTION_EX));
  alu alu_1 (.Result(alu_result), .A(read_data_1), .B(imm), .ALUSel(4'b0000));
  csr csr_1 (.tohost(tohost));  // open: CSR_address, CSR_din, CSR_WE, clk
  Multiplexer #(.enable("false"), .select(2), .width(32)) multiplexer_1 (
    .in0(alu_result), .in1(READ_DATA), .out(WRITE_DATA), .sel(2'b00));  // open: in2, in3

  assign WRITE_ADDRESS = {32{1'b0}};
  assign WRITE_ENABLE = 4'b0000;
  // also tied to GND on the sheet: {tohost[0], tohost[1], tohost[2], tohost[3], tohost[4], tohost[5], tohost[6], tohost[7], tohost[8], tohost[9], tohost[10], tohost[11], tohost[12], tohost[13], tohost[14], tohost[15], tohost[16], tohost[17], tohost[18], tohost[19], tohost[20], tohost[21], tohost[22], tohost[23], tohost[24], tohost[25], tohost[26], tohost[27], tohost[28], tohost[29], tohost[30], tohost[31]}

  // Notes on the sheet:
  //   Output to IMEM
  //   IMEM (do **NOT** move this)
  //   Inputs from IMEM
  //   It is OK to move the PC, RegFile, ALU, MEM, Branch Comp, Imm Gen, and Control Logic to wherever is most convenient for you when constructing your CPU, and to delete this text
  //   Inputs/Outputs for testing. Do **NOT** move these.
  //   Outputs To DMEM
  //   DMEM (do **NOT** move this)
  //   Inputs From DMEM
endmodule

module decode (
  input  [31:0] INST,
  output [4:0] RD,
  output [4:0] RS1,
  output [4:0] RS2
);


  assign RD = INST[11:7];
  assign RS1 = INST[19:15];
  assign RS2 = {5{1'b0}};
endmodule

module IF_EX (
  input  [31:0] PC_IN,
  input  [31:0] INST_IN,
  output [31:0] PC_OUT,
  output [31:0] INST_OUT
);

  wire CLK;

  Clock clock_1 (.out(CLK));
  Register #(.width(32)) register_1 (.D(PC_IN), .en(1'b1), .clk(CLK), .Q(PC_OUT));  // open: clr
  Register #(.width(32)) register_2 (.D(INST_IN), .en(1'b1), .clk(CLK), .Q(INST_OUT));  // open: clr
endmodule
