// Logisim project imm_gen.circ as structural Verilog: 2 circuits, main circuit imm_gen
module imm_gen (
  input  [31:0] inst,
  input  [2:0] ImmSel,
  output [31:0] imm
);

  I_imm i_imm_1 (.INST(inst), .IMM(imm));

  // Notes on the sheet:
  //   INPUTS to your circuit
  //   DON'T CHANGE THE LOCATIONS OF THE INPUTS AND OUTPUTS!
  //   OUTPUT from your circuit
endmodule

module I_imm (
  input  [31:0] INST,
  output [31:0] IMM
);

  assign IMM = {{21{INST[31]}}, INST[30:20]};  // Bit_Extender bit_extender_1
endmodule
